// Logisim project LOGISIM1.circ as structural Verilog: 1 circuit, main circuit main
module main (
  input  A1,
  input  B0,
  input  A0,
  input  B1,
  output X,
  output Y,
  output Z
);

  wire and_1_out, and_2_out, and_3_out, and_4_out, and_5_out, and_6_out, and_7_out, not_1_out, not_2_out,
       not_3_out, or_2_out, or_3_out, or_4_out;

  not not_1 (not_1_out, A0);
  and and_1 (and_1_out, A0, not_2_out);
  not not_2 (not_2_out, B0);
  and and_2 (and_2_out, B1, A1);
  and and_3 (and_3_out, not_1_out, B0);
  or or_1 (X, and_3_out, and_1_out);
  or or_2 (or_2_out, A0, B0);
  and and_4 (and_4_out, not_2_out, not_1_out);
  and and_5 (and_5_out, not_2_out, and_2_out);
  and and_6 (and_6_out, A1, B1);
  or or_3 (or_3_out, B1, A1);
  or or_4 (or_4_out, or_3_out, or_2_out);
  and and_7 (and_7_out, and_4_out, or_3_out);
  or or_5 (Y, and_6_out, not_3_out);
  not not_3 (not_3_out, or_4_out);
  or or_6 (Z, and_7_out, and_5_out);
endmodule
