// Logisim project log2_mux_dec.circ as structural Verilog: 1 circuit, main circuit main
module main (
  input  A1,
  input  A0,
  input  B1,
  input  B0,
  input  S0,
  input  S1,
  output X2,
  output X1,
  output Y0,
  output Y1,
  output Y2,
  output Y3,
  output Y4,
  output Y5,
  output Y6,
  output Y7,
  output X0
);

  wire and_1_out, and_2_out, and_3_out, and_4_out, n3_to_8_decoder_74138_2_p7, n3_to_8_decoder_74138_2_p8,
       n3_to_8_decoder_74138_3_p7, n3_to_8_decoder_74138_3_p8, n3_to_8_decoder_74138_3_p9,
       n3_to_8_decoder_74138_4_p10, n3_to_8_decoder_74138_4_p11, n3_to_8_decoder_74138_4_p12,
       n3_to_8_decoder_74138_5_p7, n3_to_8_decoder_74138_5_p9, n3_to_8_decoder_74138_5_p10,
       n3_to_8_decoder_74138_5_p11, n3_to_8_decoder_74138_5_p12, n3_to_8_decoder_74138_5_p13,
       n3_to_8_decoder_74138_5_p14, n3_to_8_decoder_74138_5_p15, n3_to_8_decoder_74138_5_p16, not_1_out,
       not_2_out, not_3_out, not_4_out, not_5_out, not_6_out, not_7_out, not_8_out, not_9_out, not_10_out,
       not_11_out, or_1_out, or_2_out, or_3_out, or_4_out, or_5_out, or_6_out, or_7_out, or_8_out, or_9_out,
       or_10_out, or_11_out, xor_1_out;

  not not_1 (not_1_out, A1);
  xor xor_1 (xor_1_out, A0, B0);
  or or_1 (or_1_out, A1, B1);
  not not_2 (not_2_out, B1);
  and and_1 (and_1_out, not_1_out, B1);
  not not_3 (not_3_out, A1);
  or or_2 (or_2_out, not_3_out, B1);
  or or_3 (or_3_out, A1, not_2_out);
  // _3_to_8_decoder__74138 #(.Facing("east")) 3_to_8_decoder_74138_1: pin names not known; wires that end beside it: A0, B1, B0
  // _3_to_8_decoder__74138 #(.Facing("east")) 3_to_8_decoder_74138_2: pin names not known; wires that end beside it: A1, A0, B0, 1'b1, 1'b0, 1'b0, n3_to_8_decoder_74138_2_p7, n3_to_8_decoder_74138_2_p8
  // _3_to_8_decoder__74138 #(.Facing("east")) 3_to_8_decoder_74138_3: pin names not known; wires that end beside it: 1'b1, 1'b0, A1, A0, B1, 1'b0, n3_to_8_decoder_74138_3_p7, n3_to_8_decoder_74138_3_p8, n3_to_8_decoder_74138_3_p9
  // _3_to_8_decoder__74138 #(.Facing("east")) 3_to_8_decoder_74138_4: pin names not known; wires that end beside it: A1, B0, B1, 1'b1, 1'b1, 1'b0, 1'b0, 1'b0, 1'b0, n3_to_8_decoder_74138_4_p10, n3_to_8_decoder_74138_4_p11, n3_to_8_decoder_74138_4_p12
  and and_2 (and_2_out, or_2_out, B0);
  and and_3 (and_3_out, A0, or_3_out);
  not not_4 (not_4_out, n3_to_8_decoder_74138_2_p7);
  or or_4 (or_4_out, and_2_out, and_3_out);
  or or_5 (or_5_out, not_4_out, not_5_out);
  not not_5 (not_5_out, n3_to_8_decoder_74138_2_p8);
  or or_6 (or_6_out, not_6_out, not_8_out);
  or or_7 (or_7_out, not_7_out, not_9_out);
  not not_6 (not_6_out, n3_to_8_decoder_74138_3_p7);
  not not_7 (not_7_out, n3_to_8_decoder_74138_3_p8);
  not not_8 (not_8_out, n3_to_8_decoder_74138_3_p9);
  not not_9 (not_9_out, n3_to_8_decoder_74138_4_p10);
  or or_8 (or_8_out, not_10_out, not_11_out);
  not not_10 (not_10_out, n3_to_8_decoder_74138_4_p11);
  not not_11 (not_11_out, n3_to_8_decoder_74138_4_p12);
  or or_9 (or_9_out, and_1_out, or_5_out);
  and and_4 (and_4_out, B0, or_6_out);
  or or_10 (or_10_out, and_4_out, or_7_out);
  or or_11 (or_11_out, or_10_out, or_8_out);
  // _4_to_1_MUX__x2___74153 #(.Facing("east")) 4_to_1_mux_x2_74153_1: pin names not known; wires that end beside it: or_11_out, or_9_out, 1'b0, B1, A1, or_11_out, or_1_out, B0, A0, 1'b0, S0, 1'b0, S1, X2, X1
  // _4_to_1_MUX__x2___74153 #(.Facing("east")) 4_to_1_mux_x2_74153_2: pin names not known; wires that end beside it: xor_1_out, or_4_out, 1'b0, 1'b1, 1'b0, S0, 1'b0, S1, X0
  // _3_to_8_decoder__74138 #(.Facing("east")) 3_to_8_decoder_74138_5: pin names not known; wires that end beside it: X0, X1, X2, 1'b1, 1'b0, 1'b0, n3_to_8_decoder_74138_5_p7, n3_to_8_decoder_74138_5_p7, n3_to_8_decoder_74138_5_p9, n3_to_8_decoder_74138_5_p10, n3_to_8_decoder_74138_5_p11, n3_to_8_decoder_74138_5_p12, n3_to_8_decoder_74138_5_p13, n3_to_8_decoder_74138_5_p14, n3_to_8_decoder_74138_5_p15, n3_to_8_decoder_74138_5_p16
  not not_12 (Y0, n3_to_8_decoder_74138_5_p9);
  not not_13 (Y1, n3_to_8_decoder_74138_5_p10);
  not not_14 (Y2, n3_to_8_decoder_74138_5_p11);
  not not_15 (Y3, n3_to_8_decoder_74138_5_p12);
  not not_16 (Y4, n3_to_8_decoder_74138_5_p13);
  not not_17 (Y5, n3_to_8_decoder_74138_5_p14);
  not not_18 (Y6, n3_to_8_decoder_74138_5_p15);
  not not_19 (Y7, n3_to_8_decoder_74138_5_p16);

  // Notes on the sheet:
  //   s=0 -> x2
  //   s=0 -> x0
  //   s=1 -> x2
  //   s=0 -> x1
  //   s=1 -> x1
  //   s=1 -> x0
  //   s=2 -> x2
  //   s=2 -> x1
  //   s=2 -> x0
  //   s=3 -> x2
  //   s=3 -> x1
  //   s=3 -> x0
endmodule
